// Logisim project Exp02_MaquinaDeEstado.circ as structural Verilog: 1 circuit, main circuit main
module main (
  input  T
);

  wire and_1_out, and_2_out, clock_1_out, d_ff_1_q, d_ff_2_q, d_ff_2_qn, xor_1_out, xor_2_out;

  Clock clock_1 (.out(clock_1_out));
  xor xor_1 (xor_1_out, d_ff_1_q, d_ff_2_q);
  xor xor_2 (xor_2_out, T, d_ff_1_q);
  and and_1 (and_1_out, T, xor_1_out);
  and and_2 (and_2_out, xor_2_out, d_ff_2_qn);
  D_Flip_Flop d_ff_1 (.clk(clock_1_out), .D(and_1_out), .Q(d_ff_1_q));  // open: Qn, preset, en, reset
  D_Flip_Flop d_ff_2 (.clk(clock_1_out), .D(and_2_out), .Q(d_ff_2_q), .Qn(d_ff_2_qn));  // open: preset, en, reset

  // Notes on the sheet:
  //   CLK
  //   B
  //   A
endmodule
