// Logisim project Aula1-Logisim.circ as structural Verilog: 1 circuit, main circuit main
module main (
  input  in_1,
  input  in_2,
  input  in_3,
  input  in_4,
  input  in_5,
  input  in_6,
  input  in_7,
  input  [1:0] in_8,
  input  in_9,
  input  in_10,
  input  in_11,
  input  in_12,
  input  [2:0] in_13,
  output out_14,
  output out_15,
  output out_16,
  output out_17,
  output out_18,
  output out_19,
  output out_20,
  output out_21
);

  wire and_1_out, clock_1_out, D0_qn, D1_qn, multiplexer_1_out, nand_1_out, nand_2_out, not_1_out, not_2_out;

  Decoder #(.select(3), .disabled(0)) decoder_1 (
    .out0(out_14), .out1(out_15), .out2(out_16), .out3(out_17), .out4(out_18), .out5(out_19), .out6(out_20),
    .out7(out_21), .sel(in_13), .en(in_12));
  not not_1 (not_1_out, in_1);
  not not_2 (not_2_out, in_2);
  Multiplexer #(.select(2), .enable("false")) multiplexer_1 (
    .in0(in_3), .in1(in_5), .in2(in_6), .in3(in_7), .out(multiplexer_1_out), .sel(in_8));
  nand nand_1 (nand_1_out, not_1_out, nand_2_out);
  nand nand_2 (nand_2_out, nand_1_out, not_2_out);
  LED led_1 (.in(multiplexer_1_out));
  LED led_2 (.in(nand_1_out));
  LED led_3 (.in(nand_2_out));
  Clock clock_1 (.out(clock_1_out));
  J_K_Flip_Flop D1 (.J(in_4), .clk(clock_1_out), .Qn(D1_qn));  // open: K, Q, preset, en, reset
  and and_1 (and_1_out, D0_qn, D1_qn);
  J_K_Flip_Flop D0 (.J(and_1_out), .clk(clock_1_out), .Q(in_4), .Qn(D0_qn));  // open: K, preset, en, reset
endmodule
