// Logisim project Aula2-Memoria_ROM.circ as structural Verilog: 1 circuit, main circuit main
module main (
  input  A,
  input  B,
  input  C,
  input  D,
  input  in_5,
  input  in_6,
  input  in_7,
  input  in_8,
  input  in_9,
  input  in_10,
  input  in_11,
  input  in_12,
  input  in_13,
  input  in_14,
  input  in_15,
  input  in_16,
  input  in_17,
  input  in_18,
  input  in_19,
  input  in_20,
  output out_21
);

  wire _0_out, _1_out, _2_out, _3_out, _4_out, _5_out, _6_out, _7_out, _8_out, _9_out, _10_out, _11_out,
       _12_out, _13_out, _14_out, _15_out, and_1_out, and_2_out, and_3_out, and_4_out, and_5_out, and_6_out,
       and_7_out, and_8_out, not_1_out, not_2_out, not_3_out, not_4_out, not_5_out, not_6_out, not_7_out,
       not_8_out;

  not not_1 (not_1_out, C);
  not not_2 (not_2_out, D);
  not not_3 (not_3_out, C);
  not not_4 (not_4_out, D);
  and and_1 (and_1_out, not_1_out, not_2_out);
  and and_2 (and_2_out, not_3_out, D);
  and and_3 (and_3_out, C, not_4_out);
  and and_4 (and_4_out, C, D);
  not not_5 (not_5_out, B);
  not not_6 (not_6_out, A);
  and and_5 (and_5_out, not_6_out, not_5_out);
  not not_7 (not_7_out, A);
  and and_6 (and_6_out, not_7_out, B);
  and _0 (_0_out, and_1_out, and_5_out, in_5);
  and _1 (_1_out, and_2_out, and_5_out, in_9);
  and _2 (_2_out, and_3_out, and_5_out, in_13);
  and _3 (_3_out, and_4_out, and_5_out, in_17);
  and _4 (_4_out, and_1_out, and_6_out, in_6);
  and _5 (_5_out, and_2_out, and_6_out, in_10);
  and _6 (_6_out, and_3_out, and_6_out, in_14);
  and _7 (_7_out, and_4_out, and_6_out, in_18);
  not not_8 (not_8_out, B);
  and and_7 (and_7_out, A, not_8_out);
  and _8 (_8_out, and_1_out, and_7_out, in_7);
  and _9 (_9_out, and_2_out, and_7_out, in_11);
  and _10 (_10_out, and_3_out, and_7_out, in_15);
  and _11 (_11_out, and_4_out, and_7_out, in_19);
  and and_8 (and_8_out, A, B);
  and _12 (_12_out, and_1_out, and_8_out, in_8);
  and _13 (_13_out, and_2_out, and_8_out, in_12);
  and _14 (_14_out, and_3_out, and_8_out, in_16);
  and _15 (_15_out, and_4_out, and_8_out, in_20);
  or or_1 (out_21, _12_out, _8_out, _4_out, _0_out, _13_out, _9_out, _5_out, _1_out, _14_out, _10_out, _6_out, _2_out, _15_out, _11_out, _7_out, _3_out);
endmodule
